// Logisim project master.circ as structural Verilog: 25 circuits, main circuit FullAdder
module HalfAdder (
  input  A,
  input  B,
  output Sum,
  output Cout
);

  xor xor_1 (Sum, A, B);
  and and_1 (Cout, A, B);
endmodule

module FullAdder (
  input  A,
  input  B,
  input  Cin,
  output Sum,
  output Cout
);

  wire and_1_out, and_2_out, and_3_out, xor_1_out;

  and and_1 (and_1_out, B, Cin);
  and and_2 (and_2_out, A, Cin);
  and and_3 (and_3_out, A, B);
  or or_1 (Cout, and_1_out, and_2_out, and_3_out);
  xor xor_1 (xor_1_out, A, B);
  xor xor_2 (Sum, xor_1_out, Cin);
endmodule

module FullSubtractor (
  input  A,
  input  B,
  input  Bin,
  output Sum,
  output Bout
);

  wire and_1_out, and_2_out, and_3_out, not_1_out, not_2_out, xor_1_out;

  and and_1 (and_1_out, B, Bin);
  not not_1 (not_1_out, A);
  and and_2 (and_2_out, not_1_out, Bin);
  not not_2 (not_2_out, A);
  and and_3 (and_3_out, not_2_out, B);
  or or_1 (Bout, and_1_out, and_2_out, and_3_out);
  xor xor_1 (xor_1_out, A, B);
  xor xor_2 (Sum, xor_1_out, Bin);
endmodule

module OnesComp (
  input  [3:0] A,
  output [3:0] R
);

  not not_1 (R[0], A[0]);
  not not_2 (R[1], A[1]);
  not not_3 (R[2], A[2]);
  not not_4 (R[3], A[3]);
endmodule

module TwosComp (
  input  [3:0] A,
  output [3:0] R,
  output Overflow
);

  wire fulladder_1_cout, fulladder_2_cout, fulladder_3_cout;
  wire [3:0] onescomp_1_r;

  OnesComp onescomp_1 (.A(A), .R(onescomp_1_r));
  FullAdder fulladder_1 (.A(1'b1), .B(onescomp_1_r[0]), .Sum(R[0]), .Cout(fulladder_1_cout));  // open: Cin
  FullAdder fulladder_2 (.A(onescomp_1_r[1]), .Cin(fulladder_1_cout), .Sum(R[1]), .Cout(fulladder_2_cout));  // open: B
  FullAdder fulladder_3 (.A(onescomp_1_r[2]), .Cin(fulladder_2_cout), .Sum(R[2]), .Cout(fulladder_3_cout));  // open: B
  FullAdder fulladder_4 (.A(onescomp_1_r[3]), .Cin(fulladder_3_cout), .Sum(R[3]), .Cout(Overflow));  // open: B
endmodule

module FourBitAdder (
  input  [3:0] Add1,
  input  [3:0] Add2,
  output [3:0] AddOut
);

  wire fulladder_2_cout, fulladder_3_cout, fulladder_4_cout;

  FullAdder fulladder_1 (.A(Add1[3]), .B(Add2[3]), .Cin(fulladder_2_cout), .Sum(AddOut[3]));  // open: Cout
  FullAdder fulladder_2 (.A(Add1[2]), .B(Add2[2]), .Cin(fulladder_3_cout), .Sum(AddOut[2]), .Cout(fulladder_2_cout));
  FullAdder fulladder_3 (.A(Add1[1]), .B(Add2[1]), .Cin(fulladder_4_cout), .Sum(AddOut[1]), .Cout(fulladder_3_cout));
  FullAdder fulladder_4 (.A(Add1[0]), .B(Add2[0]), .Sum(AddOut[0]), .Cout(fulladder_4_cout));  // open: Cin
endmodule

module FourBitSubtractor (
  input  [3:0] Subtract1,
  input  [3:0] Subtract2,
  output [3:0] SubtractOut
);

  wire fullsubtractor_2_bout, fullsubtractor_3_bout, fullsubtractor_4_bout;

  FullSubtractor fullsubtractor_1 (
    .A(Subtract1[3]), .B(Subtract2[3]), .Bin(fullsubtractor_2_bout), .Sum(SubtractOut[3]));  // open: Bout
  FullSubtractor fullsubtractor_2 (
    .A(Subtract1[2]), .B(Subtract2[2]), .Bin(fullsubtractor_3_bout), .Sum(SubtractOut[2]),
    .Bout(fullsubtractor_2_bout));
  FullSubtractor fullsubtractor_3 (
    .A(Subtract1[1]), .B(Subtract2[1]), .Bin(fullsubtractor_4_bout), .Sum(SubtractOut[1]),
    .Bout(fullsubtractor_3_bout));
  FullSubtractor fullsubtractor_4 (
    .A(Subtract1[0]), .B(Subtract2[0]), .Sum(SubtractOut[0]), .Bout(fullsubtractor_4_bout));  // open: Bin
endmodule

module SR_Latch (
  input  Reset,
  input  Set,
  output Q,
  output NOT_Q
);

  nor nor_1 (Q, Reset, NOT_Q);
  nor nor_2 (NOT_Q, Q, Set);
endmodule

module Clocked_SR_Latch (
  input  Set,
  input  Reset,
  input  Clk,
  output Q,
  output NOT_Q
);

  wire nand_1_out, nand_2_out;

  nand nand_1 (nand_1_out, Set, Clk);
  nand nand_2 (nand_2_out, Clk, Reset);
  nand nand_3 (Q, nand_1_out, NOT_Q);
  nand nand_4 (NOT_Q, Q, nand_2_out);
endmodule

module D_Latch (
  input  D,
  input  Clk,
  output Q,
  output NOT_Q
);

  wire not_1_out;

  not not_1 (not_1_out, D);
  Clocked_SR_Latch clocked_sr_latch_1 (.Set(D), .Reset(not_1_out), .Clk(Clk), .Q(Q), .NOT_Q(NOT_Q));
endmodule

module SR_FlipFlop (
  input  Set,
  input  Reset,
  input  Clk,
  output Q,
  output NOT_Q
);

  wire clocked_sr_latch_1_not_q, clocked_sr_latch_1_q, not_1_out, not_2_out;

  not not_1 (not_1_out, Clk);
  Clocked_SR_Latch clocked_sr_latch_1 (
    .Set(Set), .Reset(Reset), .Clk(not_1_out), .Q(clocked_sr_latch_1_q), .NOT_Q(clocked_sr_latch_1_not_q));
  not not_2 (not_2_out, not_1_out);
  Clocked_SR_Latch clocked_sr_latch_2 (
    .Set(clocked_sr_latch_1_q), .Reset(clocked_sr_latch_1_not_q), .Clk(not_2_out), .Q(Q), .NOT_Q(NOT_Q));

  // Notes on the sheet:
  //   Rising Edge
  //   Falling Edge
endmodule

module D_FlipFlop (
  input  D,
  input  Clk,
  output Q,
  output NOT_Q
);

  wire d_latch_1_not_q, d_latch_1_q, not_1_out, not_2_out;

  not not_1 (not_1_out, Clk);
  D_Latch d_latch_1 (.D(D), .Clk(not_1_out), .Q(d_latch_1_q), .NOT_Q(d_latch_1_not_q));
  not not_2 (not_2_out, not_1_out);
  Clocked_SR_Latch clocked_sr_latch_1 (
    .Set(d_latch_1_q), .Reset(d_latch_1_not_q), .Clk(not_2_out), .Q(Q), .NOT_Q(NOT_Q));

  // Notes on the sheet:
  //   Rising Edge
  //   Falling Edge
endmodule

module JK_FlipFlop (
  input  J,
  input  K,
  input  Clk,
  output Q,
  output NOT_Q
);

  wire and_1_out, and_2_out, not_1_out, or_1_out;

  not not_1 (not_1_out, K);
  and and_1 (and_1_out, NOT_Q, J);
  or or_1 (or_1_out, and_1_out, and_2_out);
  and and_2 (and_2_out, not_1_out, Q);
  D_Flip_Flop d_ff_1 (.D(or_1_out), .clk(Clk), .Q(Q), .Qn(NOT_Q));  // open: preset, reset
endmodule

module T_FlipFlop (
  input  T,
  input  Clk,
  output Q,
  output NOT_Q
);

  wire xor_1_out;

  xor xor_1 (xor_1_out, Q, T);
  D_Flip_Flop d_ff_1 (.D(xor_1_out), .clk(Clk), .Q(Q), .Qn(NOT_Q));  // open: preset, reset
endmodule

module TwoBitRegister (
  input  In0,
  input  In1,
  input  Reset,
  input  Clk,
  output Y0,
  output Y1
);

  D_Flip_Flop d_ff_1 (.D(In0), .clk(Clk), .Q(Y0), .reset(Reset));  // open: Qn, preset
  D_Flip_Flop d_ff_2 (.D(In1), .clk(Clk), .Q(Y1), .reset(Reset));  // open: Qn, preset
endmodule

module FourBitRegister (
  input  In0,
  input  In1,
  input  In2,
  input  In3,
  input  Reset,
  input  Clk,
  output Y0,
  output Y1,
  output Y2,
  output Y3
);

  D_Flip_Flop A0 (.D(In0), .clk(Clk), .Q(Y0), .reset(Reset));  // open: Qn, preset
  D_Flip_Flop A1 (.D(In1), .clk(Clk), .Q(Y1), .reset(Reset));  // open: Qn, preset
  D_Flip_Flop A2 (.D(In2), .clk(Clk), .Q(Y2), .reset(Reset));  // open: Qn, preset
  D_Flip_Flop A3 (.D(In3), .clk(Clk), .Q(Y3), .reset(Reset));  // open: Qn, preset
endmodule

module FourBitRegisterWithLoad (
  input  In0,
  input  In1,
  input  In2,
  input  In3,
  input  Load,
  input  Reset,
  input  Clk,
  output Y0,
  output Y1,
  output Y2,
  output Y3
);

  wire multiplexer_1_out, multiplexer_2_out, multiplexer_3_out, multiplexer_4_out;

  Multiplexer multiplexer_1 (.in0(Y0), .in1(In0), .out(multiplexer_1_out), .sel(Load));
  Multiplexer multiplexer_2 (.in0(Y1), .in1(In1), .out(multiplexer_2_out), .sel(Load));
  Multiplexer multiplexer_3 (.in0(Y2), .in1(In2), .out(multiplexer_3_out), .sel(Load));
  Multiplexer multiplexer_4 (.in0(Y3), .in1(In3), .out(multiplexer_4_out), .sel(Load));
  FourBitRegister fourbitregister_1 (
    .In0(multiplexer_1_out), .In1(multiplexer_2_out), .In2(multiplexer_3_out), .In3(multiplexer_4_out),
    .Reset(Reset), .Clk(Clk), .Y0(Y0), .Y1(Y1), .Y2(Y2), .Y3(Y3));
endmodule

module FourBitRightShiftRegister (
  input  Data_In,
  input  Clk,
  output Out0,
  output Out1,
  output Out2,
  output Out3
);

  D_Flip_Flop d_ff_1 (.D(Data_In), .clk(Clk), .Q(Out3));  // open: Qn, preset, reset
  D_Flip_Flop d_ff_2 (.D(Out3), .clk(Clk), .Q(Out2));  // open: Qn, preset, reset
  D_Flip_Flop d_ff_3 (.D(Out2), .clk(Clk), .Q(Out1));  // open: Qn, preset, reset
  D_Flip_Flop d_ff_4 (.D(Out1), .clk(Clk), .Q(Out0));  // open: Qn, preset, reset
endmodule

module FourBitLeftShiftRegister (
  input  Data_In,
  input  Clk,
  output Out0,
  output Out1,
  output Out2,
  output Out3
);

  D_Flip_Flop d_ff_1 (.D(Out2), .clk(Clk), .Q(Out3));  // open: Qn, preset, reset
  D_Flip_Flop d_ff_2 (.D(Out1), .clk(Clk), .Q(Out2));  // open: Qn, preset, reset
  D_Flip_Flop d_ff_3 (.D(Out0), .clk(Clk), .Q(Out1));  // open: Qn, preset, reset
  D_Flip_Flop d_ff_4 (.D(Data_In), .clk(Clk), .Q(Out0));  // open: Qn, preset, reset
endmodule

module FourBitParallelLoad (
  input  Shift,
  input  Load,
  input  Serial_In,
  input  D0,
  input  D1,
  input  D2,
  input  D3,
  input  Clk,
  output Q0,
  output Q1,
  output Q2,
  output Q3
);

  wire multiplexer_1_out, multiplexer_2_out, multiplexer_3_out, multiplexer_4_out;

  Multiplexer #(.select(2)) multiplexer_1 (
    .in0(Q0), .in1(Serial_In), .in2(D0), .out(multiplexer_1_out), .sel({Load, Shift}));  // open: in3
  Multiplexer #(.select(2)) multiplexer_2 (
    .in0(Q1), .in1(Q0), .in2(D1), .out(multiplexer_2_out), .sel({Load, Shift}));  // open: in3
  Multiplexer #(.select(2)) multiplexer_3 (
    .in0(Q2), .in1(Q1), .in2(D2), .out(multiplexer_3_out), .sel({Load, Shift}));  // open: in3
  Multiplexer #(.select(2)) multiplexer_4 (
    .in0(Q3), .in1(Q2), .in2(D3), .out(multiplexer_4_out), .sel({Load, Shift}));  // open: in3
  D_Flip_Flop d_ff_1 (.D(multiplexer_1_out), .clk(Clk), .Q(Q0));  // open: Qn, preset, reset
  D_Flip_Flop d_ff_2 (.D(multiplexer_2_out), .clk(Clk), .Q(Q1));  // open: Qn, preset, reset
  D_Flip_Flop d_ff_3 (.D(multiplexer_3_out), .clk(Clk), .Q(Q2));  // open: Qn, preset, reset
  D_Flip_Flop d_ff_4 (.D(multiplexer_4_out), .clk(Clk), .Q(Q3));  // open: Qn, preset, reset

  // Notes on the sheet:
  //   Shift = Select_0
  //   Load = Select_1
  //   If Select == 3, unused
  //   If Select == 0, loop the flip-flop back on itself
  //   If Select == 2, put D0, D1, D2, D3 into each register
  //   If Select == 1, output of the current flip-flop goes to the next flip-flop
endmodule

module SRAM_Integrated_Circuit (
  input  Selectt,
  input  Clock,
  input  B,
  input  NOT_B,
  input  Reset,
  output C,
  output NOT_C
);

  wire and_1_out, and_2_out, s_r_ff_1_q, s_r_ff_1_qn;

  and and_1 (and_1_out, B, Selectt);
  and and_2 (and_2_out, Selectt, NOT_B);
  S_R_Flip_Flop #(.trigger("high")) s_r_ff_1 (
    .S(and_1_out), .R(and_2_out), .clk(Clock), .Q(s_r_ff_1_q), .reset(Reset), .Qn(s_r_ff_1_qn));  // open: preset
  and and_3 (C, s_r_ff_1_q, Selectt);
  and and_4 (NOT_C, Selectt, s_r_ff_1_qn);

  // Notes on the sheet:
  //   Select acts like an address in memory
  //   This circuit stores a one bit data inside of an "address"
endmodule

module SRAM_1_Bit_Word (
  input  WordSelect_0,
  input  WordSelect_1,
  input  WordSelect_2,
  input  WordSelect_3,
  input  Data_In,
  input  WriteOrRead,
  input  Bit_Select,
  input  Reset,
  input  Clock,
  output Data_Out
);

  wire and_1_out, and_2_out, and_3_out, not_1_out, not_2_out, or_1_out, or_2_out, s_r_ff_1_q,
       sram_integrated_circuit_1_c, sram_integrated_circuit_1_not_c, sram_integrated_circuit_2_c,
       sram_integrated_circuit_2_not_c, sram_integrated_circuit_3_c, sram_integrated_circuit_3_not_c,
       sram_integrated_circuit_4_c, sram_integrated_circuit_4_not_c;

  and and_1 (and_1_out, Data_In, and_2_out);
  and and_2 (and_2_out, not_1_out, Bit_Select);
  not not_1 (not_1_out, WriteOrRead);
  and and_3 (and_3_out, and_2_out, not_2_out);
  not not_2 (not_2_out, Data_In);
  SRAM_Integrated_Circuit sram_integrated_circuit_1 (
    .Selectt(WordSelect_0), .Clock(Clock), .B(and_1_out), .NOT_B(and_3_out), .Reset(Reset),
    .C(sram_integrated_circuit_1_c), .NOT_C(sram_integrated_circuit_1_not_c));
  SRAM_Integrated_Circuit sram_integrated_circuit_2 (
    .Selectt(WordSelect_1), .Clock(Clock), .B(and_1_out), .NOT_B(and_3_out), .Reset(Reset),
    .C(sram_integrated_circuit_2_c), .NOT_C(sram_integrated_circuit_2_not_c));
  SRAM_Integrated_Circuit sram_integrated_circuit_3 (
    .Selectt(WordSelect_2), .Clock(Clock), .B(and_1_out), .NOT_B(and_3_out), .Reset(Reset),
    .C(sram_integrated_circuit_3_c), .NOT_C(sram_integrated_circuit_3_not_c));
  SRAM_Integrated_Circuit sram_integrated_circuit_4 (
    .Selectt(WordSelect_3), .Clock(Clock), .B(and_1_out), .NOT_B(and_3_out), .Reset(Reset),
    .C(sram_integrated_circuit_4_c), .NOT_C(sram_integrated_circuit_4_not_c));
  or or_1 (or_1_out, sram_integrated_circuit_4_not_c, sram_integrated_circuit_3_not_c, sram_integrated_circuit_2_not_c, sram_integrated_circuit_1_not_c);
  or or_2 (or_2_out, sram_integrated_circuit_4_c, sram_integrated_circuit_3_c, sram_integrated_circuit_2_c, sram_integrated_circuit_1_c);
  S_R_Flip_Flop #(.trigger("high")) s_r_ff_1 (
    .S(or_2_out), .R(or_1_out), .clk(Clock), .Q(s_r_ff_1_q));  // open: reset, Qn, preset
  and and_4 (Data_Out, s_r_ff_1_q, Bit_Select);

  // Notes on the sheet:
  //   Word Select acts like an address selector
  //   You're only allowed to select one word at a time
  //   You can read or write data from/to an address using these params
endmodule

module Ram_4_Word_1_Bit (
  input  A0,
  input  A1,
  input  Data_In,
  input  WriteOrRead,
  input  Bit_Select,
  input  Reset,
  input  Clock,
  output Data_Out
);

  wire decoder_1_out0, decoder_1_out1, decoder_1_out2, decoder_1_out3, sram_1_bit_word_1_data_out;

  Decoder #(.select(2)) decoder_1 (
    .out0(decoder_1_out0), .out1(decoder_1_out1), .out2(decoder_1_out2), .out3(decoder_1_out3), .sel({A1, A0}));  // open: en
  assign Data_Out = Bit_Select ? sram_1_bit_word_1_data_out : 1'bz;  // Controlled_Buffer controlled_buffer_1
  SRAM_1_Bit_Word sram_1_bit_word_1 (
    .WordSelect_0(decoder_1_out0), .WordSelect_1(decoder_1_out1), .WordSelect_2(decoder_1_out2),
    .WordSelect_3(decoder_1_out3), .Data_In(Data_In), .WriteOrRead(WriteOrRead), .Bit_Select(Bit_Select),
    .Reset(Reset), .Clock(Clock), .Data_Out(sram_1_bit_word_1_data_out));

  // Notes on the sheet:
  //   Word Selector
endmodule

module Ram_16_Word_1_Bit (
  input  [3:0] A,
  input  Data_In,
  input  WriteOrRead,
  input  Bit_Select,
  input  Reset,
  input  Clock,
  output Data_Out
);

  wire decoder_1_out0, decoder_1_out1, decoder_1_out2, decoder_1_out3, decoder_1_out4, decoder_1_out5,
       decoder_1_out6, decoder_1_out7, decoder_1_out8, decoder_1_out9, decoder_1_out10, decoder_1_out11,
       decoder_1_out12, decoder_1_out13, decoder_1_out14, decoder_1_out15, decoder_2_out0, decoder_2_out1,
       decoder_2_out2, decoder_2_out3, or_1_out, sram_1_bit_word_1_data_out, sram_1_bit_word_2_data_out,
       sram_1_bit_word_3_data_out, sram_1_bit_word_4_data_out;

  Decoder #(.select(4)) decoder_1 (
    .out0(decoder_1_out0), .out1(decoder_1_out1), .out2(decoder_1_out2), .out3(decoder_1_out3),
    .out4(decoder_1_out4), .out5(decoder_1_out5), .out6(decoder_1_out6), .out7(decoder_1_out7),
    .out8(decoder_1_out8), .out9(decoder_1_out9), .out10(decoder_1_out10), .out11(decoder_1_out11),
    .out12(decoder_1_out12), .out13(decoder_1_out13), .out14(decoder_1_out14), .out15(decoder_1_out15),
    .sel(A));  // open: en
  Decoder #(.select(2)) decoder_2 (
    .out0(decoder_2_out0), .out1(decoder_2_out1), .out2(decoder_2_out2), .out3(decoder_2_out3), .sel(A[3:2]),
    .en(Bit_Select));
  SRAM_1_Bit_Word sram_1_bit_word_1 (
    .WordSelect_0(decoder_1_out0), .WordSelect_1(decoder_1_out1), .WordSelect_2(decoder_1_out2),
    .WordSelect_3(decoder_1_out3), .Data_In(Data_In), .WriteOrRead(WriteOrRead), .Bit_Select(decoder_2_out0),
    .Reset(Reset), .Clock(Clock), .Data_Out(sram_1_bit_word_1_data_out));
  SRAM_1_Bit_Word sram_1_bit_word_2 (
    .WordSelect_0(decoder_1_out4), .WordSelect_1(decoder_1_out5), .WordSelect_2(decoder_1_out6),
    .WordSelect_3(decoder_1_out7), .Data_In(Data_In), .WriteOrRead(WriteOrRead), .Bit_Select(decoder_2_out1),
    .Reset(Reset), .Clock(Clock), .Data_Out(sram_1_bit_word_2_data_out));
  SRAM_1_Bit_Word sram_1_bit_word_3 (
    .WordSelect_0(decoder_1_out8), .WordSelect_1(decoder_1_out9), .WordSelect_2(decoder_1_out10),
    .WordSelect_3(decoder_1_out11), .Data_In(Data_In), .WriteOrRead(WriteOrRead),
    .Bit_Select(decoder_2_out2), .Reset(Reset), .Clock(Clock), .Data_Out(sram_1_bit_word_3_data_out));
  SRAM_1_Bit_Word sram_1_bit_word_4 (
    .WordSelect_0(decoder_1_out12), .WordSelect_1(decoder_1_out13), .WordSelect_2(decoder_1_out14),
    .WordSelect_3(decoder_1_out15), .Data_In(Data_In), .WriteOrRead(WriteOrRead),
    .Bit_Select(decoder_2_out3), .Reset(Reset), .Clock(Clock), .Data_Out(sram_1_bit_word_4_data_out));
  or or_1 (or_1_out, sram_1_bit_word_1_data_out, sram_1_bit_word_2_data_out, sram_1_bit_word_3_data_out, sram_1_bit_word_4_data_out);
  assign Data_Out = Bit_Select ? or_1_out : 1'bz;  // Controlled_Buffer controlled_buffer_1

  // Notes on the sheet:
  //   Bit Select Decoder
endmodule

module Ram_16_Word_1_Bit_With_2_Decoder (
  input  [3:0] A,
  input  Data_In,
  input  WriteOrRead,
  input  Chip_Select,
  input  Reset,
  input  Clock,
  output Data_Out
);

  wire decoder_1_out0, decoder_1_out1, decoder_1_out2, decoder_1_out3, decoder_2_out0, decoder_2_out1,
       decoder_2_out2, decoder_2_out3, or_1_out, sram_1_bit_word_1_data_out, sram_1_bit_word_2_data_out,
       sram_1_bit_word_3_data_out, sram_1_bit_word_4_data_out;

  Decoder #(.select(2)) decoder_1 (
    .out0(decoder_1_out0), .out1(decoder_1_out1), .out2(decoder_1_out2), .out3(decoder_1_out3), .sel(A[3:2]));  // open: en
  Decoder #(.select(2)) decoder_2 (
    .out0(decoder_2_out0), .out1(decoder_2_out1), .out2(decoder_2_out2), .out3(decoder_2_out3), .sel(A[1:0]),
    .en(Chip_Select));
  SRAM_1_Bit_Word sram_1_bit_word_1 (
    .WordSelect_0(decoder_1_out0), .WordSelect_1(decoder_1_out1), .WordSelect_2(decoder_1_out2),
    .WordSelect_3(decoder_1_out3), .Data_In(Data_In), .WriteOrRead(WriteOrRead), .Bit_Select(decoder_2_out0),
    .Reset(Reset), .Clock(Clock), .Data_Out(sram_1_bit_word_1_data_out));
  SRAM_1_Bit_Word sram_1_bit_word_2 (
    .WordSelect_0(decoder_1_out0), .WordSelect_1(decoder_1_out1), .WordSelect_2(decoder_1_out2),
    .WordSelect_3(decoder_1_out3), .Data_In(Data_In), .WriteOrRead(WriteOrRead), .Bit_Select(decoder_2_out1),
    .Reset(Reset), .Clock(Clock), .Data_Out(sram_1_bit_word_2_data_out));
  SRAM_1_Bit_Word sram_1_bit_word_3 (
    .WordSelect_0(decoder_1_out0), .WordSelect_1(decoder_1_out1), .WordSelect_2(decoder_1_out2),
    .WordSelect_3(decoder_1_out3), .Data_In(Data_In), .WriteOrRead(WriteOrRead), .Bit_Select(decoder_2_out2),
    .Reset(Reset), .Clock(Clock), .Data_Out(sram_1_bit_word_3_data_out));
  SRAM_1_Bit_Word sram_1_bit_word_4 (
    .WordSelect_0(decoder_1_out0), .WordSelect_1(decoder_1_out1), .WordSelect_2(decoder_1_out2),
    .WordSelect_3(decoder_1_out3), .Data_In(Data_In), .WriteOrRead(WriteOrRead), .Bit_Select(decoder_2_out3),
    .Reset(Reset), .Clock(Clock), .Data_Out(sram_1_bit_word_4_data_out));
  or or_1 (or_1_out, sram_1_bit_word_4_data_out, sram_1_bit_word_3_data_out, sram_1_bit_word_2_data_out, sram_1_bit_word_1_data_out);
  assign Data_Out = Chip_Select ? or_1_out : 1'bz;  // Controlled_Buffer controlled_buffer_1

  // Notes on the sheet:
  //   Row Select (Word Select)
  //   Column Select (Bit Select)
endmodule
